# Fritzing sketch Octo_v1.0 Altered By CommanderWolfyX (saved by Fritzing 0.9.3b)
circuit board: 8.7cm x 4.27612cm
breadboards: 2

parts:
  Part1 = Adafruit TCA9548A
  TP1 = TP4056 [chip_label=TP4056 package="DIP (Dual Inline) [THT]"]
  WeMos_D1_Mini1 = WeMos D1 Mini
  D1 = Rectifier Diode [part_number=1N5817 package="300 mil [THT]"]
  D2 = Rectifier Diode [part_number=1N5817 package="300 mil [THT]"]
  180K = Resistor [tolerance=±5% resistance=180k package=THT]
  Bat_-_+ = female pin header, 2 pins [form="♀ (female)"]
  Switch = female pin header, 3 pins [form="♀ (female)"]
  J3 = female pin header, 4 pins [form="♀ (female)"]
  J4 = female pin header, 4 pins [form="♀ (female)"]
  J5 = female pin header, 4 pins [form="♀ (female)"]
  J6 = female pin header, 4 pins [form="♀ (female)"]
  J7 = female pin header, 4 pins [form="♀ (female)"]
  J8 = female pin header, 4 pins [form="♀ (female)"]
  J9 = female pin header, 4 pins [form="♀ (female)"]
  J10 = female pin header, 4 pins [form="♀ (female)"]
  J11 = female pin header, 4 pins [form="♀ (female)"]
  LCD = female pin header, 4 pins [form="♀ (female)"]
  J12 = female pin header, 12 pins [form="♀ (female)"]

nets:
  N1: Part1.2SDA, J9.pin3, J12.pin1
  N2: Part1.2SCL, J9.pin1, J12.pin2
  N3: Part1.3SDA, J8.pin3, J12.pin3
  N4: Part1.3SCL, J8.pin1, J12.pin4
  N5: Part1.4SDA, J7.pin3, J12.pin5
  N6: Part1.4SCL, J7.pin1, J12.pin6
  N7: Part1.5SDA, J6.pin3, J12.pin7
  N8: Part1.5SCL, J6.pin1, J12.pin8
  N9: Part1.6SDA, J5.pin3, J12.pin9
  N10: Part1.6SCL, J5.pin1, J12.pin10
  N11: Part1.7SDA, J4.pin3, J12.pin11
  N12: Part1.7SCL, J4.pin1, J12.pin12
  VCC: Part1.VCC, Part1.RESET, WeMos_D1_Mini1.5V, D1.cathode, D2.cathode, J4.pin2, J5.pin2, J6.pin2, J7.pin2, J8.pin2, J9.pin2, J10.pin2, J11.pin2, LCD.pin4
  N13: Part1.GND, Part1.A0, Part1.A1, Part1.A2, WeMos_D1_Mini1.G, Switch.pin1, J3.pin2, J4.pin4, J5.pin4, J6.pin4, J7.pin4, J8.pin4, J9.pin4, J10.pin4, J11.pin4, LCD.pin3
  N14: Part1.INPUTSDA, WeMos_D1_Mini1.D2, LCD.pin1
  N15: Part1.INPUTSCL, WeMos_D1_Mini1.D1, LCD.pin2
  N16: Part1.0SDA, J11.pin3
  N17: Part1.0SCL, J11.pin1
  N18: Part1.1SDA, J10.pin3
  N19: Part1.1SCL, J10.pin1
  N20: TP1.pin1, D1.anode
  N21: TP1.pin3, D2.anode
  N22: TP1.pin4, 180K.Pin_1, Bat_-_+.pin2
  N23: TP1.pin5, Bat_-_+.pin1
  N24: TP1.pin6, Switch.pin2
  N25: WeMos_D1_Mini1.A0, 180K.Pin_0
  N26: WeMos_D1_Mini1.D6, J3.pin1
  N27: WeMos_D1_Mini1.D7, J3.pin3
  N28: WeMos_D1_Mini1.D8, J3.pin4

notes:
  Octo Slime
  By EmbeddedAT.com
  V1.0

custom parts:
  Adafruit TCA9548A: You just found the perfect I2C sensor, and you want to wire up two or three or more of them to your Arduino when you realize "Uh oh, this chip has a fixed I2C address, and from what I know about I2C, you cannot have two devices with the same address on the same SDA/SCL pins!" Are you out of luck? You would be, if you didn't have this ultra-cool TCA9548A 1-to-8 I2C multiplexer! Finally, a way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
  TP4056: A DIP stand-in part for whatever IC you want. With 6 pins on a 300mil dual inline package (DIP) footprint.
  WeMos D1 Mini: The D1 mini is a mini wifi board based on ESP-8266EX.
